// Logisim project Project2ZacharyWillson.circ as structural Verilog: 4 circuits, main circuit main
module main (
);

  wire and_1_out, and_2_out, B0, B1, B2, B3, B4, B5, B6, B7, B8, B9, BL, BU, C0, C1, C2, CLK, L1_l, L1_u,
       not_1_out, or_8_out, P1_v, R0, R1, R3, R4, Valid;
  wire [2:0] counter_1_q;
  wire [3:0] IB1_c0, P1_b0, register_2_q, register_3_q, register_4_q, register_5_q;

  Button n1 (.out(B1));
  Button n4 (.out(B4));
  Button n7 (.out(B7));
  Button L (.out(BL));
  Button n3 (.out(B3));
  Button n2 (.out(B2));
  Button n6 (.out(B6));
  Button n5 (.out(B5));
  Button n9 (.out(B9));
  Button n8 (.out(B8));
  Button U (.out(BU));
  Button n0 (.out(B0));
  or or_1 (R0, B3, B2, B1);
  or or_2 (R1, B6, B5, B4);
  or or_3 (R3, B9, B8, B7);
  or or_4 (R4, BU, B0, BL);
  or or_5 (C0, B1, B4, B7, BL);
  or or_6 (C1, B2, B5, B8, B0);
  or or_7 (C2, B3, B6, B9, BU);
  Clock clock_1 (.out(CLK));
  nand nand_1 (Valid, IB1_c0[0], IB1_c0[1], IB1_c0[2], IB1_c0[3]);
  // Probe on P1_b0
  Panel P1 (
    .R0(R0), .R1(R1), .R2(R3), .R3(R4), .C0(C0), .C1(C1), .C2(C2), .B0(P1_b0[0]), .B1(P1_b0[1]),
    .B2(P1_b0[2]), .B3(P1_b0[3]), .V(P1_v));
  LED Press (.in(P1_v));
  // Probe on IB1_c0
  InputBuffer IB1 (
    .B0(P1_b0[0]), .B1(P1_b0[1]), .B2(P1_b0[2]), .B3(P1_b0[3]), .V(P1_v), .CLK(not_1_out), .C0(IB1_c0[0]),
    .C1(IB1_c0[1]), .C2(IB1_c0[2]), .C3(IB1_c0[3]));
  not not_1 (not_1_out, CLK);
  Register #(.width(4)) register_1 (.D(register_2_q), .en(Valid), .clk(CLK));  // open: Q, clr
  Lock L1 (.C0(IB1_c0[0]), .C1(IB1_c0[1]), .C2(IB1_c0[2]), .C3(IB1_c0[3]), .CLK(CLK), .L(L1_l), .U(L1_u));
  Counter #(.max('h7), .width(3)) counter_1 (
    .count(or_8_out), .Q(counter_1_q), .up(L1_u), .clk(CLK));  // open: load, D, carry, clr
  or or_8 (or_8_out, L1_l, L1_u);
  Register #(.width(4)) register_2 (.D(register_3_q), .en(Valid), .clk(CLK), .Q(register_2_q));  // open: clr
  LED Unlocked (.in(and_1_out));
  and and_1 (and_1_out, ~counter_1_q[0], ~counter_1_q[1], ~counter_1_q[2]);  // AND_Gate
  Register #(.width(4)) register_3 (.D(register_4_q), .en(Valid), .clk(CLK), .Q(register_3_q));  // open: clr
  LED Locked (.in(and_2_out));
  and and_2 (and_2_out, ~counter_1_q[0], ~counter_1_q[1], counter_1_q[2]);  // AND_Gate
  Register #(.width(4)) register_4 (.D(register_5_q), .en(Valid), .clk(CLK), .Q(register_4_q));  // open: clr
  Register #(.width(4)) register_5 (.D(IB1_c0), .en(Valid), .clk(CLK), .Q(register_5_q));  // open: clr
endmodule

module Panel (
  input  R0,
  input  R1,
  input  R2,
  input  R3,
  input  C0,
  input  C1,
  input  C2,
  output B0,
  output B1,
  output B2,
  output B3,
  output V
);

  wire di1, di2, di3, di4, di5, di6, di7, di8, di9, L, not_1_out, not_2_out, not_3_out, not_4_out, not_5_out,
       not_6_out, not_7_out, not_8_out, not_9_out, not_10_out, not_11_out, not_12_out, not_13_out,
       not_14_out, not_15_out, not_16_out, not_17_out, not_18_out, not_19_out, not_20_out, not_21_out,
       not_22_out, not_23_out, not_24_out, not_25_out, not_26_out, not_27_out, not_28_out, not_29_out,
       not_30_out, not_31_out, not_32_out, not_33_out, not_34_out, not_35_out, not_36_out, not_37_out,
       not_38_out, not_39_out, not_40_out, not_41_out, not_42_out, not_43_out, not_44_out, not_45_out,
       not_46_out, not_47_out, not_48_out, not_49_out, not_50_out, not_51_out, not_52_out, not_53_out,
       not_54_out, not_55_out, not_56_out, not_57_out, not_58_out, not_59_out, not_60_out, U, zero;

  not not_1 (not_1_out, R1);
  not not_2 (not_2_out, R2);
  not not_3 (not_3_out, R3);
  not not_4 (not_4_out, C1);
  not not_5 (not_5_out, C2);
  not not_6 (not_6_out, R1);
  not not_7 (not_7_out, R2);
  not not_8 (not_8_out, R3);
  not not_9 (not_9_out, C0);
  not not_10 (not_10_out, C2);
  not not_11 (not_11_out, R1);
  not not_12 (not_12_out, R2);
  not not_13 (not_13_out, R3);
  not not_14 (not_14_out, C0);
  not not_15 (not_15_out, C1);
  not not_16 (not_16_out, R2);
  not not_17 (not_17_out, R3);
  not not_18 (not_18_out, C1);
  not not_19 (not_19_out, C2);
  not not_20 (not_20_out, R0);
  not not_21 (not_21_out, R2);
  not not_22 (not_22_out, R3);
  not not_23 (not_23_out, C0);
  not not_24 (not_24_out, C1);
  and di_1 (di1, R0, not_1_out, not_2_out, not_3_out, C0, not_4_out, not_5_out);
  and di_2 (di2, R0, not_6_out, not_7_out, not_8_out, not_9_out, C1, not_10_out);
  and di_3 (di3, R0, not_11_out, not_12_out, not_13_out, not_14_out, not_15_out, C2);
  not not_25 (not_25_out, R0);
  and di_4 (di4, not_25_out, R1, not_16_out, not_17_out, C0, not_18_out, not_19_out);
  not not_26 (not_26_out, R0);
  not not_27 (not_27_out, R2);
  not not_28 (not_28_out, R3);
  and di_5 (di5, not_26_out, R1, not_27_out, not_28_out, not_29_out, C1, not_30_out);
  not not_29 (not_29_out, C0);
  not not_30 (not_30_out, C2);
  and di_6 (di6, not_20_out, R1, not_21_out, not_22_out, not_23_out, not_24_out, C2);
  not not_31 (not_31_out, R0);
  not not_32 (not_32_out, R1);
  not not_33 (not_33_out, R3);
  and di_7 (di7, not_31_out, not_32_out, R2, not_33_out, C0, not_34_out, not_35_out);
  not not_34 (not_34_out, C1);
  not not_35 (not_35_out, C2);
  not not_36 (not_36_out, R0);
  not not_37 (not_37_out, R1);
  not not_38 (not_38_out, R3);
  and di_8 (di8, not_36_out, not_37_out, R2, not_38_out, not_39_out, C1, not_40_out);
  not not_39 (not_39_out, C0);
  not not_40 (not_40_out, C2);
  not not_41 (not_41_out, R0);
  not not_42 (not_42_out, R1);
  not not_43 (not_43_out, R3);
  and di_9 (di9, not_41_out, not_42_out, R2, not_43_out, not_44_out, not_45_out, C2);
  not not_44 (not_44_out, C0);
  not not_45 (not_45_out, C1);
  not not_46 (not_46_out, R0);
  not not_47 (not_47_out, R1);
  not not_48 (not_48_out, R2);
  and u_L (L, not_46_out, not_47_out, not_48_out, R3, C0, not_49_out, not_50_out);
  not not_49 (not_49_out, C1);
  not not_50 (not_50_out, C2);
  not not_51 (not_51_out, R0);
  not not_52 (not_52_out, R1);
  not not_53 (not_53_out, R2);
  and u_zero (zero, not_51_out, not_52_out, not_53_out, R3, not_54_out, C1, not_55_out);
  not not_54 (not_54_out, C0);
  not not_55 (not_55_out, C2);
  not not_56 (not_56_out, R0);
  not not_57 (not_57_out, R1);
  not not_58 (not_58_out, R2);
  not not_59 (not_59_out, C0);
  not not_60 (not_60_out, C1);
  and u_U (U, not_56_out, not_57_out, not_58_out, R3, not_59_out, not_60_out, C2);
  Priority_Encoder #(.select(4)) priority_encoder_1 (
    .in0(zero), .in1(di1), .in2(di2), .in3(di3), .in4(di4), .in5(di5), .in6(di6), .in7(di7), .in8(di8),
    .in9(di9), .in10(L), .in11(U), .out({B3, B2, B1, B0}), .en_in(V));  // open: in12, in13, in14, in15, gs, en_out
  ExactlyOne xor_1 (
    .out(V), .in0(di1), .in1(di2), .in2(di3), .in3(di4), .in4(di5), .in5(di6), .in6(di7), .in7(di8),
    .in8(di9), .in9(zero), .in10(L), .in11(U));
endmodule

module InputBuffer (
  input  B0,
  input  B1,
  input  B2,
  input  B3,
  input  V,
  input  CLK,
  output C0,
  output C1,
  output C2,
  output C3
);

  wire and_1_out, d_ff_1_q, V_Rising, xor_1_out;

  D_Flip_Flop d_ff_1 (.D(V), .clk(CLK), .Q(d_ff_1_q));  // open: Qn, preset, reset
  xor xor_1 (xor_1_out, V, d_ff_1_q);
  and and_1 (and_1_out, xor_1_out, V);
  D_Flip_Flop d_ff_2 (.D(and_1_out), .clk(CLK), .Q(V_Rising));  // open: Qn, preset, reset
  Multiplexer #(.width(4)) multiplexer_1 (
    .in0(4'b1111), .in1({B3, B2, B1, B0}), .out({C3, C2, C1, C0}), .sel(V_Rising));
endmodule

module Lock (
  input  C0,
  input  C1,
  input  C2,
  input  C3,
  input  CLK,
  output L,
  output U
);

  wire and_1_out, and_2_out, and_3_out, and_4_out, and_25_out, and_26_out, and_27_out, CODE_SET,
       CODES_ARE_EQUAL, D_1_BUFFER_SET, D_1_COMPARE_ENABLE, D_2_BUFFER_SET, D_2_COMPARE_ENABLE,
       decoder_1_out3, Digit, I_0, I_1, Lock, LOCK_SIGNAL_a, LOCK_SIGNAL_b, LOCK_SIGNAL_c, LOCK_SIGNAL_d,
       Locked, LOCKED_BASE, LOCKED_D_1, LOCKED_D_2, LOCKED_S0_RESET, LOCKED_S0_RESET_b, LOCKED_S0_RESET_c,
       LOCKED_S0_RESET_d, LOCKED_S0_SET, LOCKED_S0_SET_a, LOCKED_S0_SET_c, LOCKED_S1_RESET,
       LOCKED_S1_RESET_b, LOCKED_S1_RESET_e, LOCKED_S1_SET, LOCKED_State_0, LOCKED_State_1, LOCKED_U_1,
       Locking, LOCKING_State_0, LOCKING_State_1, META_S0_RESET_b, META_S0_SET_a, META_S0_SET_c,
       Meta_State_0, Meta_State_1, not_1_out, NOT_I_0, NOT_I_1, or_3_out, or_4_out, or_5_out, or_6_out,
       or_11_out, or_14_out, or_15_out, or_16_out, or_17_out, or_18_out, or_19_out, Unlock, UNLOCK_SIGNAL_a,
       UNLOCK_SIGNAL_b, UNLOCK_SIGNAL_c, Unlocked, UNLOCKED_BASE, UNLOCKED_D_1, UNLOCKED_D_2, UNLOCKED_L_1,
       UNLOCKED_S0_RESET_c, UNLOCKED_S0_RESET_e, UNLOCKED_S0_SET_a, UNLOCKED_S0_SET_c, UNLOCKED_S1_RESET_b,
       UNLOCKED_S1_RESET_d, UNLOCKED_State_0, UNLOCKED_State_1, Unlocking, UNLOCKING_S0_RESET,
       UNLOCKING_S0_SET, UNLOCKING_S1_RESET, UNLOCKING_S1_SET, UNLOCKING_State_0, UNLOCKING_State_1;
  wire [3:0] D_1_BUFF_OUT, D_1_CODE_OUTPUT, D_1_COMPARE_OUTPUT, D_2_BUFF_OUT, D_2_CODE_OUTPUT,
       D_2_COMPARE_OUTPUT, D_3_CODE_OUTPUT, xnor_1_out, xnor_2_out, xnor_3_out;

  not not_1 (not_1_out, C0);
  Demultiplexer #(.select(2)) demultiplexer_1 (
    .out0(Unlocked), .out1(Locking), .out2(Locked), .out3(Unlocking), .in(1'b1),
    .sel({Meta_State_1, Meta_State_0}));
  and and_1 (and_1_out, C3, C2);
  and and_2 (and_2_out, C3, C1, C0);
  and and_3 (and_3_out, C3, C2);
  and and_4 (and_4_out, C3, C1, not_1_out);
  or or_1 (I_1, and_1_out, and_2_out);
  or or_2 (I_0, and_3_out, and_4_out);
  buf or_3 (or_3_out, META_S0_RESET_b);  // OR_Gate
  buf or_4 (or_4_out, D_1_BUFFER_SET);  // OR_Gate
  or or_5 (or_5_out, UNLOCKED_S0_RESET_e, UNLOCKED_S1_RESET_d, CODE_SET, UNLOCKED_S1_RESET_b, UNLOCKED_S0_SET_c);
  buf or_6 (or_6_out, LOCK_SIGNAL_b);  // OR_Gate
  Register #(.trigger("falling"), .width(4)) register_1 (
    .D({C3, C2, C1, C0}), .clk(D_1_BUFFER_SET), .Q(D_1_BUFF_OUT));  // open: en, clr
  and and_5 (D_2_BUFFER_SET, UNLOCKED_D_1, Digit);
  and and_6 (UNLOCKED_S0_SET_c, UNLOCKED_D_1, Lock);
  and and_7 (UNLOCKED_S1_RESET_b, UNLOCKED_D_1, Unlock);
  and and_8 (CODE_SET, UNLOCKED_D_2, Digit);
  and and_9 (UNLOCKED_S1_RESET_d, UNLOCKED_D_2, Lock);
  and and_10 (UNLOCKED_S0_RESET_e, UNLOCKED_D_2, Unlock);
  or or_7 (L, LOCK_SIGNAL_a, LOCK_SIGNAL_b, LOCK_SIGNAL_c, LOCK_SIGNAL_d);
  buf or_8 (LOCKED_S1_SET, D_1_COMPARE_ENABLE);  // OR_Gate
  Register #(.trigger("falling"), .width(4)) register_2 (
    .D({C3, C2, C1, C0}), .clk(D_1_COMPARE_ENABLE), .Q(D_1_COMPARE_OUTPUT));  // open: en, clr
  and and_11 (LOCKED_S0_SET_a, LOCKED_BASE, Unlock);
  and and_12 (D_1_COMPARE_ENABLE, LOCKED_U_1, Digit);
  and and_13 (LOCKED_S0_RESET_b, LOCKED_U_1, Lock);
  and and_14 (D_2_COMPARE_ENABLE, LOCKED_D_1, Digit);
  and and_15 (LOCKED_S1_RESET_b, LOCKED_D_1, Lock);
  and and_16 (LOCKED_S0_SET_c, LOCKED_D_1, Unlock);
  and and_17 (LOCKED_S0_RESET_c, LOCKED_D_2, Digit);
  and and_18 (LOCKED_S0_RESET_d, LOCKED_D_2, Lock);
  and and_19 (LOCKED_S1_RESET_e, LOCKED_D_2, Unlock);
  or or_9 (U, UNLOCK_SIGNAL_a, UNLOCK_SIGNAL_b, UNLOCK_SIGNAL_c, META_S0_RESET_b);
  buf or_10 (UNLOCKING_S1_SET, UNLOCK_SIGNAL_b);  // OR_Gate
  not not_2 (NOT_I_1, I_1);
  not not_3 (NOT_I_0, I_0);
  buf or_11 (or_11_out, LOCK_SIGNAL_d);  // OR_Gate
  S_R_Flip_Flop #(.trigger("falling")) s_r_ff_1 (
    .S(or_11_out), .R(or_3_out), .clk(CLK), .Q(Meta_State_1));  // open: reset, Qn, preset
  S_R_Flip_Flop #(.trigger("falling")) s_r_ff_2 (
    .S(or_4_out), .R(or_5_out), .clk(CLK), .Q(UNLOCKED_State_1));  // open: reset, Qn, preset
  S_R_Flip_Flop #(.trigger("falling")) s_r_ff_3 (
    .S(or_6_out), .R(LOCK_SIGNAL_d), .clk(CLK), .Q(LOCKING_State_1));  // open: reset, Qn, preset
  and and_20 (UNLOCKED_S0_SET_a, UNLOCKED_BASE, Lock);
  and and_21 (D_1_BUFFER_SET, UNLOCKED_L_1, Digit);
  and and_22 (META_S0_SET_a, UNLOCKED_L_1, Lock);
  and and_23 (UNLOCKED_S0_RESET_c, UNLOCKED_L_1, Unlock);
  assign xnor_1_out = ~(D_2_COMPARE_OUTPUT ^ D_2_CODE_OUTPUT);  // XNOR_Gate xnor_1, 4 bits wide
  assign xnor_2_out = ~(D_3_CODE_OUTPUT ^ {C3, C2, C1, C0});  // XNOR_Gate xnor_2, 4 bits wide
  and and_24 (META_S0_SET_c, CODES_ARE_EQUAL, LOCKED_S0_RESET_c);
  Register #(.trigger("falling"), .width(4)) register_3 (
    .D({C3, C2, C1, C0}), .clk(D_2_BUFFER_SET), .Q(D_2_BUFF_OUT));  // open: en, clr
  assign xnor_3_out = ~(D_1_COMPARE_OUTPUT ^ D_1_CODE_OUTPUT);  // XNOR_Gate xnor_3, 4 bits wide
  Decoder #(.enable("false"), .select(2)) decoder_1 (
    .out0(Digit), .out1(Lock), .out2(Unlock), .out3(decoder_1_out3), .sel({I_1, I_0}));
  Register #(.trigger("falling"), .width(4)) register_4 (
    .D({C3, C2, C1, C0}), .clk(D_2_COMPARE_ENABLE), .Q(D_2_COMPARE_OUTPUT));  // open: en, clr
  Demultiplexer #(.select(2)) demultiplexer_2 (
    .out0(UNLOCKED_BASE), .out1(UNLOCKED_L_1), .out2(UNLOCKED_D_1), .out3(UNLOCKED_D_2), .in(Unlocked),
    .sel({UNLOCKED_State_1, UNLOCKED_State_0}));
  Demultiplexer #(.select(2)) demultiplexer_3 (
    .out0(LOCK_SIGNAL_a), .out1(LOCK_SIGNAL_b), .out2(LOCK_SIGNAL_c), .out3(LOCK_SIGNAL_d), .in(Locking),
    .sel({LOCKING_State_1, LOCKING_State_0}));
  Demultiplexer #(.select(2)) demultiplexer_4 (
    .out0(LOCKED_BASE), .out1(LOCKED_U_1), .out2(LOCKED_D_1), .out3(LOCKED_D_2), .in(Locked),
    .sel({LOCKED_State_1, LOCKED_State_0}));
  Demultiplexer #(.select(2)) demultiplexer_5 (
    .out0(UNLOCK_SIGNAL_a), .out1(UNLOCK_SIGNAL_b), .out2(UNLOCK_SIGNAL_c), .out3(META_S0_RESET_b),
    .in(Unlocking), .sel({UNLOCKING_State_1, UNLOCKING_State_0}));
  and and_25 (and_25_out, xnor_3_out[0], xnor_3_out[1], xnor_3_out[2], xnor_3_out[3]);
  and and_26 (and_26_out, xnor_1_out[0], xnor_1_out[1], xnor_1_out[2], xnor_1_out[3]);
  and and_27 (and_27_out, xnor_2_out[0], xnor_2_out[1], xnor_2_out[2], xnor_2_out[3]);
  LED u_Digit (.in(Digit));
  LED u_Lock (.in(Lock));
  LED u_Unlock (.in(Unlock));
  LED Invalid (.in(decoder_1_out3));
  or or_12 (LOCKED_S1_RESET, LOCKED_S0_SET_c, LOCKED_S1_RESET_b, LOCKED_S0_RESET_c, LOCKED_S1_RESET_e);
  buf or_13 (UNLOCKING_S1_RESET, META_S0_RESET_b);  // OR_Gate
  and and_28 (CODES_ARE_EQUAL, and_25_out, and_26_out, and_27_out);
  or or_14 (or_14_out, UNLOCKED_S0_SET_a, D_2_BUFFER_SET, UNLOCKED_S0_SET_c);
  or or_15 (or_15_out, UNLOCKED_S0_RESET_e, CODE_SET, META_S0_SET_a, D_1_BUFFER_SET);
  or or_16 (or_16_out, LOCK_SIGNAL_b, LOCK_SIGNAL_d);
  S_R_Flip_Flop #(.trigger("falling")) s_r_ff_4 (
    .S(or_14_out), .R(or_15_out), .clk(CLK), .Q(UNLOCKED_State_0));  // open: reset, Qn, preset
  or or_17 (or_17_out, LOCK_SIGNAL_a, LOCK_SIGNAL_c);
  S_R_Flip_Flop #(.trigger("falling")) s_r_ff_5 (
    .S(or_17_out), .R(or_16_out), .clk(CLK), .Q(LOCKING_State_0));  // open: reset, Qn, preset
  Register #(.trigger("falling"), .width(4)) register_5 (
    .D(D_1_BUFF_OUT), .clk(CODE_SET), .Q(D_1_CODE_OUTPUT));  // open: en, clr
  or or_18 (or_18_out, META_S0_SET_a, CODE_SET, META_S0_SET_c);
  or or_19 (or_19_out, LOCK_SIGNAL_d, META_S0_RESET_b);
  or or_20 (LOCKED_S0_SET, LOCKED_S0_SET_a, D_2_COMPARE_ENABLE, LOCKED_S0_SET_c);
  S_R_Flip_Flop #(.trigger("falling")) s_r_ff_6 (
    .S(or_18_out), .R(or_19_out), .clk(CLK), .Q(Meta_State_0));  // open: reset, Qn, preset
  or or_21 (UNLOCKING_S0_SET, UNLOCK_SIGNAL_a, UNLOCK_SIGNAL_c);
  Register #(.trigger("falling"), .width(4)) register_6 (
    .D(D_2_BUFF_OUT), .clk(CODE_SET), .Q(D_2_CODE_OUTPUT));  // open: en, clr
  Register #(.trigger("falling"), .width(4)) register_7 (
    .D({C3, C2, C1, C0}), .clk(CODE_SET), .Q(D_3_CODE_OUTPUT));  // open: en, clr
  or or_22 (LOCKED_S0_RESET, D_1_COMPARE_ENABLE, LOCKED_S0_RESET_b, LOCKED_S0_RESET_c, LOCKED_S0_RESET_d);
  S_R_Flip_Flop #(.trigger("falling")) s_r_ff_7 (
    .S(LOCKED_S1_SET), .R(LOCKED_S1_RESET), .clk(CLK), .Q(LOCKED_State_1));  // open: reset, Qn, preset
  S_R_Flip_Flop #(.trigger("falling")) s_r_ff_8 (
    .S(UNLOCKING_S1_SET), .R(UNLOCKING_S1_RESET), .clk(CLK), .Q(UNLOCKING_State_1));  // open: reset, Qn, preset
  or or_23 (UNLOCKING_S0_RESET, UNLOCK_SIGNAL_b, META_S0_RESET_b);
  S_R_Flip_Flop #(.trigger("falling")) s_r_ff_9 (
    .S(LOCKED_S0_SET), .R(LOCKED_S0_RESET), .clk(CLK), .Q(LOCKED_State_0));  // open: reset, Qn, preset
  S_R_Flip_Flop #(.trigger("falling")) s_r_ff_10 (
    .S(UNLOCKING_S0_SET), .R(UNLOCKING_S0_RESET), .clk(CLK), .Q(UNLOCKING_State_0));  // open: reset, Qn, preset

  // Other names for the same wires on the sheet: LOCKING_BASE = LOCK_SIGNAL_a; LOCKING_S0_SET_a = LOCK_SIGNAL_a;
  //   LOCKING_1 = LOCK_SIGNAL_b; LOCKING_S0_RESET_a = LOCK_SIGNAL_b; LOCKING_S1_SET_a = LOCK_SIGNAL_b;
  //   LOCKING_2 = LOCK_SIGNAL_c; LOCKING_S0_SET_b = LOCK_SIGNAL_c; LOCKED_S0_SET_b = D_2_COMPARE_ENABLE;
  //   LOCKED_S1_RESET_a = LOCKED_S0_SET_c; LOCKED_S1_RESET_c = LOCKED_S0_RESET_c;
  //   LOCKED_S1_RESET_d = LOCKED_S0_RESET_d; LOCKED_S0_RESET_a = D_1_COMPARE_ENABLE;
  //   LOCKED_S1_SET_a = D_1_COMPARE_ENABLE; LOCKING_3 = LOCK_SIGNAL_d; LOCKING_S0_RESET_b = LOCK_SIGNAL_d;
  //   LOCKING_S1_RESET_a = LOCK_SIGNAL_d; META_S0_RESET_a = LOCK_SIGNAL_d; META_S1_SET_a = LOCK_SIGNAL_d;
  //   UNLOCKING_BASE = UNLOCK_SIGNAL_a; UNLOCKING_S0_SET_a = UNLOCK_SIGNAL_a; UNLOCKING_1 = UNLOCK_SIGNAL_b;
  //   UNLOCKING_S0_RESET_a = UNLOCK_SIGNAL_b; UNLOCKING_S1_SET_a = UNLOCK_SIGNAL_b; UNLOCKING_2 = UNLOCK_SIGNAL_c;
  //   UNLOCKING_S0_SET_b = UNLOCK_SIGNAL_c; META_S1_RESET_a = META_S0_RESET_b; UNLOCK_SIGNAL_d = META_S0_RESET_b;
  //   UNLOCKING_3 = META_S0_RESET_b; UNLOCKING_S0_RESET_b = META_S0_RESET_b; UNLOCKING_S1_RESET_a = META_S0_RESET_b;
  //   UNLOCKED_S0_RESET_b = META_S0_SET_a; UNLOCKED_S0_SET_b = D_2_BUFFER_SET;
  //   UNLOCKED_S1_RESET_a = UNLOCKED_S0_SET_c; META_S0_SET_b = CODE_SET; UNLOCKED_S0_RESET_d = CODE_SET;
  //   UNLOCKED_S1_RESET_c = CODE_SET; UNLOCKED_S1_RESET_e = UNLOCKED_S0_RESET_e; UNLOCKED_S0_RESET_a = D_1_BUFFER_SET;
  //   UNLOCKED_S1_SET_a = D_1_BUFFER_SET
endmodule
